# Fritzing sketch Strander (saved by Fritzing 0.8.7b)
circuit board: 5.43852cm x 4.81974cm
breadboards: 1

parts:
  SparkFun_Pro_Mini_5V_16MHz = Arduino Pro Mini v13
  Raspberry_Pi_B_rev1 = Raspberry Pi B rev2
  J1 = shrouded pin header, 6 pins [form="♂ (shrouded male)"]
  J2 = shrouded pin header, 6 pins [form="♂ (shrouded male)"]
  J3 = shrouded pin header, 6 pins [form="♂ (shrouded male)"]
  Pwr = Power plug
  CONN1 = USB connector [package=THT]
  JP1 = Header 3 [package=jst-3-pth]  # not connected

nets (from the schematic view):
  N1: SparkFun_Pro_Mini_5V_16MHz.D0/TX, Raspberry_Pi_B_rev1.GPIO_15
  N2: SparkFun_Pro_Mini_5V_16MHz.D1/RX, Raspberry_Pi_B_rev1.GPIO_14
  VCC: SparkFun_Pro_Mini_5V_16MHz.VCC, J1.pin4, J1.pin5, J2.pin4, J2.pin5, J3.pin4, J3.pin5, Pwr.VCC, CONN1.5V
  GND: SparkFun_Pro_Mini_5V_16MHz.GND, J1.pin1, J1.pin2, J1.pin3, J2.pin2, J2.pin3, Pwr.GND, CONN1.GND, CONN1.chassis5, CONN1.chassis6
  N3: SparkFun_Pro_Mini_5V_16MHz.D4, J3.pin6
  N4: SparkFun_Pro_Mini_5V_16MHz.D3_PWM, J2.pin6
  N5: SparkFun_Pro_Mini_5V_16MHz.D2, J1.pin6
  N6: Raspberry_Pi_B_rev1.GND, J3.pin1
  N7: J2.pin1, J3.pin2, J3.pin3
