# Fritzing sketch PiLone rev C 3v low spec (saved by Fritzing 0.8.7b)
circuit board: 3.15774cm x 3.39745cm
breadboards: 1

parts:
  ProMini_3V_8MHz = Arduino Pro Mini v13
  J1 = male pin header, 4 pins [form="♂ (male)"]
  J3 = male pin header, 4 pins [form="♂ (male)"]
  J2 = male pin header, 4 pins [form="♂ (male)"]
  Raspberry_Pi_B_rev1 = Raspberry Pi B rev2
  PWR_IN = mystery part, 2 pins [chip_label="PWR IN 5V"]
  PWR_OUT = mystery part, 2 pins [chip_label="PWR OUT 5V"]

nets:
  N1: ProMini_3V_8MHz.D0/TX, Raspberry_Pi_B_rev1.GPIO_15
  N2: ProMini_3V_8MHz.D1/RX, Raspberry_Pi_B_rev1.GPIO_14
  N3: ProMini_3V_8MHz.VCC, J1.pin3, J3.pin3, J2.pin3, PWR_IN.pin1, PWR_OUT.pin1
  GND: ProMini_3V_8MHz.GND, J1.pin1, J1.pin4, J3.pin1, J3.pin4, J2.pin1, J2.pin4, Raspberry_Pi_B_rev1.GND, PWR_IN.pin2, PWR_OUT.pin2
  N4: ProMini_3V_8MHz.D4, J3.pin2
  N5: ProMini_3V_8MHz.D3_PWM, J2.pin2
  N6: ProMini_3V_8MHz.D2, J1.pin2

notes:
  <->
  PiLone
  Rev C 3V
  solder USB micro cable here
  Power In
