# Fritzing sketch PiLone rev C (saved by Fritzing 0.8.7b)
circuit board: 4.25cm x 3.7cm
breadboards: 1

parts:
  ProMini_5V_16MHz = Arduino Pro Mini v13
  Pwr = Power plug
  J1 = male pin header, 4 pins [form="♂ (male)"]
  J3 = male pin header, 4 pins [form="♂ (male)"]
  J2 = male pin header, 4 pins [form="♂ (male)"]
  USB = USB connector [package=THT]
  Raspberry_Pi_B_rev1 = Raspberry Pi B rev2

nets:
  N1: ProMini_5V_16MHz.D0/TX, Raspberry_Pi_B_rev1.GPIO_14
  N2: ProMini_5V_16MHz.D1/RX, Raspberry_Pi_B_rev1.GPIO_15
  VCC: ProMini_5V_16MHz.VCC, Pwr.VCC, J1.pin3, J3.pin3, J2.pin3, USB.5V
  GND: ProMini_5V_16MHz.GND, Pwr.GND, J1.pin1, J1.pin4, J3.pin1, J3.pin4, J2.pin1, J2.pin4, USB.GND, USB.chassis5, USB.chassis6, Raspberry_Pi_B_rev1.GND
  N3: ProMini_5V_16MHz.D4, J3.pin2
  N4: ProMini_5V_16MHz.D3_PWM, J2.pin2
  N5: ProMini_5V_16MHz.D2, J1.pin2

notes:
  <->
  7,54€ par 12
  PiLone
  Rev C
