# Fritzing sketch PiLone rev D 3v low spec (saved by Fritzing 0.8.7b)
circuit board: 2.82662cm x 3.92035cm
breadboards: 1

parts:
  J1 = male pin header, 4 pins [form="♂ (male)"]
  J3 = male pin header, 4 pins [form="♂ (male)"]
  J2 = male pin header, 4 pins [form="♂ (male)"]
  Raspberry_Pi_B_rev1 = Raspberry Pi B rev2
  ProMini_3V_8MHz = Arduino Pro Mini v13
  F1 = Resettable Fuse PTC [part_number=1100mA package=ptc]
  5V = mystery part, 2 pins [chip_label=5V]
  JP1 = mystery part, 2 pins [chip_label="Fuse bypass"]
  D1 = Diode [package=diode-1n4001]
  C1 = Electrolytic Capacitor [capacitance=0.22mF package="100 mil [THT, electrolytic]"]

nets:
  GND: J1.pin1, J1.pin4, J3.pin1, J3.pin4, J2.pin1, J2.pin4, Raspberry_Pi_B_rev1.GND, ProMini_3V_8MHz.GND, 5V.pin2, D1.A, C1.-
  N1: J1.pin2, ProMini_3V_8MHz.D2
  N2: J1.pin3, J3.pin3, J2.pin3, ProMini_3V_8MHz.RAW, F1.1, 5V.pin1, JP1.pin1, D1.C, C1.+
  N3: J3.pin2, ProMini_3V_8MHz.D4
  N4: J2.pin2, ProMini_3V_8MHz.D3_PWM
  N5: Raspberry_Pi_B_rev1.5V, F1.2, JP1.pin2
  N6: Raspberry_Pi_B_rev1.GPIO_14, ProMini_3V_8MHz.D1/RX
  N7: Raspberry_Pi_B_rev1.GPIO_15, ProMini_3V_8MHz.D0/TX

notes:
  Power In
  PiLone
  Rev D 3V
